// Logisim project ABC3.circ as structural Verilog: 6 circuits, main circuit main
module main (
  input  B4,
  input  B3,
  input  B2,
  input  B1,
  input  B0,
  output out_6,
  output out_7,
  output Dont_care_Nah_ah,
  output out_9,
  output out_10
);

  \Остаток_2  \u_остаток_2_1  (.B0(B0), .B1(B1), .B2(B2), .B3(B3), .B4(B4), .R1(out_6), .Dont_care(Dont_care_Nah_ah));
  \Остаток_1  \u_остаток_1_1  (.B0(B0), .B1(B1), .B2(B2), .B3(B3), .B4(B4), .Dont_care(Dont_care_Nah_ah), .R1(out_7));
  \_1_нуль  \u_1_нуль_1  (.B0(B0), .B1(B1), .B2(B2), .B3(B3), .B4(B4), .Dont_care(Dont_care_Nah_ah), .R1(out_9));
  \_2_нуля  \u_2_нуля_1  (.B0(B0), .B1(B1), .B2(B2), .B3(B3), .B4(B4), .R1(out_10), .Dont_care(Dont_care_Nah_ah));

  // Notes on the sheet:
  //   Остаток деления на 3
  //   Кол-во нулей не граничащих друг с другом
endmodule

module \Остаток_2  (
  input  B0,
  input  B1,
  input  B2,
  input  B3,
  input  B4,
  output R1,
  output Dont_care
);

  wire and_1_out, and_2_out, and_3_out, and_4_out, and_5_out, and_6_out, and_7_out, and_8_out, and_9_out,
       and_10_out, and_11_out, controlled_buffer_1_out, controlled_buffer_2_out, controlled_buffer_3_out,
       controlled_buffer_4_out, controlled_buffer_5_out, nor_1_out, nor_2_out, not_1_out, not_2_out,
       not_3_out, not_4_out, not_5_out, not_6_out, not_7_out, not_8_out, not_9_out, not_10_out, not_11_out,
       not_12_out, not_13_out, not_14_out, not_15_out, not_16_out, not_17_out, not_18_out, not_19_out,
       not_20_out, not_21_out, not_22_out, not_23_out, not_24_out, not_25_out;

  and and_1 (and_1_out, B0, B1, B2, B3, B4);
  nor nor_1 (nor_1_out, B0, B1, B2, B3, B4);
  nor nor_2 (nor_2_out, and_1_out, nor_1_out);
  or or_1 (Dont_care, nor_1_out, and_1_out);
  assign controlled_buffer_1_out = nor_2_out ? B3 : 1'bz;  // Controlled_Buffer controlled_buffer_1
  assign controlled_buffer_2_out = nor_2_out ? B4 : 1'bz;  // Controlled_Buffer controlled_buffer_2
  assign controlled_buffer_3_out = nor_2_out ? B0 : 1'bz;  // Controlled_Buffer controlled_buffer_3
  assign controlled_buffer_4_out = nor_2_out ? B1 : 1'bz;  // Controlled_Buffer controlled_buffer_4
  assign controlled_buffer_5_out = nor_2_out ? B2 : 1'bz;  // Controlled_Buffer controlled_buffer_5
  not not_1 (not_1_out, controlled_buffer_2_out);
  not not_2 (not_2_out, controlled_buffer_1_out);
  not not_3 (not_3_out, controlled_buffer_5_out);
  not not_4 (not_4_out, controlled_buffer_3_out);
  not not_5 (not_5_out, controlled_buffer_2_out);
  not not_6 (not_6_out, controlled_buffer_1_out);
  not not_7 (not_7_out, controlled_buffer_4_out);
  not not_8 (not_8_out, controlled_buffer_2_out);
  not not_9 (not_9_out, controlled_buffer_5_out);
  not not_10 (not_10_out, controlled_buffer_4_out);
  not not_11 (not_11_out, controlled_buffer_3_out);
  not not_12 (not_12_out, controlled_buffer_5_out);
  not not_13 (not_13_out, controlled_buffer_2_out);
  not not_14 (not_14_out, controlled_buffer_2_out);
  not not_15 (not_15_out, controlled_buffer_3_out);
  not not_16 (not_16_out, controlled_buffer_1_out);
  not not_17 (not_17_out, controlled_buffer_5_out);
  not not_18 (not_18_out, controlled_buffer_4_out);
  not not_19 (not_19_out, controlled_buffer_1_out);
  not not_20 (not_20_out, controlled_buffer_4_out);
  not not_21 (not_21_out, controlled_buffer_3_out);
  not not_22 (not_22_out, controlled_buffer_1_out);
  not not_23 (not_23_out, controlled_buffer_5_out);
  not not_24 (not_24_out, controlled_buffer_3_out);
  not not_25 (not_25_out, controlled_buffer_4_out);
  and and_2 (and_2_out, not_1_out, not_2_out, not_3_out, controlled_buffer_4_out, not_4_out);
  and and_3 (and_3_out, not_5_out, not_6_out, controlled_buffer_5_out, not_7_out, controlled_buffer_3_out);
  and and_4 (and_4_out, not_8_out, controlled_buffer_1_out, not_9_out, not_10_out, not_11_out);
  and and_5 (and_5_out, controlled_buffer_1_out, not_12_out, controlled_buffer_4_out, controlled_buffer_3_out, not_13_out);
  and and_6 (and_6_out, not_14_out, controlled_buffer_1_out, controlled_buffer_5_out, controlled_buffer_4_out, not_15_out);
  and and_7 (and_7_out, controlled_buffer_2_out, not_16_out, not_17_out, not_18_out, controlled_buffer_3_out);
  and and_8 (and_8_out, controlled_buffer_2_out, not_19_out, controlled_buffer_5_out, not_20_out, not_21_out);
  and and_9 (and_9_out, controlled_buffer_2_out, not_22_out, controlled_buffer_5_out, controlled_buffer_4_out, controlled_buffer_3_out);
  and and_10 (and_10_out, controlled_buffer_2_out, controlled_buffer_1_out, not_23_out, controlled_buffer_4_out, not_24_out);
  and and_11 (and_11_out, controlled_buffer_2_out, controlled_buffer_1_out, controlled_buffer_5_out, not_25_out, controlled_buffer_3_out);
  or or_2 (R1, and_2_out, and_3_out, and_4_out, and_5_out, and_6_out, and_7_out, and_8_out, and_9_out, and_10_out, and_11_out);
endmodule

module \Остаток_1  (
  input  B0,
  input  B1,
  input  B2,
  input  B3,
  input  B4,
  output Dont_care,
  output R1
);

  wire and_1_out, and_2_out, and_3_out, and_4_out, and_5_out, and_6_out, and_7_out, and_8_out, and_9_out,
       and_10_out, and_11_out, and_12_out, controlled_buffer_1_out, controlled_buffer_2_out,
       controlled_buffer_3_out, controlled_buffer_4_out, controlled_buffer_5_out, nor_1_out, nor_2_out,
       not_1_out, not_2_out, not_3_out, not_4_out, not_5_out, not_6_out, not_7_out, not_8_out, not_9_out,
       not_10_out, not_11_out, not_12_out, not_13_out, not_14_out, not_15_out, not_16_out, not_17_out,
       not_18_out, not_19_out, not_20_out, not_21_out, not_22_out, not_23_out, not_24_out, not_25_out,
       not_26_out, not_27_out, not_28_out, not_29_out, not_30_out, not_31_out;

  and and_1 (and_1_out, B4, B3, B2, B1, B0);
  nor nor_1 (nor_1_out, B4, B0, B3, B2, B1);
  nor nor_2 (nor_2_out, and_1_out, nor_1_out);
  or or_1 (Dont_care, nor_1_out, and_1_out);
  assign controlled_buffer_1_out = nor_2_out ? B4 : 1'bz;  // Controlled_Buffer controlled_buffer_1
  assign controlled_buffer_2_out = nor_2_out ? B0 : 1'bz;  // Controlled_Buffer controlled_buffer_2
  assign controlled_buffer_3_out = nor_2_out ? B1 : 1'bz;  // Controlled_Buffer controlled_buffer_3
  assign controlled_buffer_4_out = nor_2_out ? B2 : 1'bz;  // Controlled_Buffer controlled_buffer_4
  assign controlled_buffer_5_out = nor_2_out ? B3 : 1'bz;  // Controlled_Buffer controlled_buffer_5
  not not_1 (not_1_out, controlled_buffer_1_out);
  not not_2 (not_2_out, controlled_buffer_5_out);
  not not_3 (not_3_out, controlled_buffer_4_out);
  not not_4 (not_4_out, controlled_buffer_3_out);
  not not_5 (not_5_out, controlled_buffer_1_out);
  not not_6 (not_6_out, controlled_buffer_5_out);
  not not_7 (not_7_out, controlled_buffer_3_out);
  not not_8 (not_8_out, controlled_buffer_2_out);
  not not_9 (not_9_out, controlled_buffer_1_out);
  not not_10 (not_10_out, controlled_buffer_5_out);
  not not_11 (not_11_out, controlled_buffer_1_out);
  not not_12 (not_12_out, controlled_buffer_4_out);
  not not_13 (not_13_out, controlled_buffer_2_out);
  not not_14 (not_14_out, controlled_buffer_1_out);
  not not_15 (not_15_out, controlled_buffer_3_out);
  not not_16 (not_16_out, controlled_buffer_5_out);
  not not_17 (not_17_out, controlled_buffer_4_out);
  not not_18 (not_18_out, controlled_buffer_3_out);
  not not_19 (not_19_out, controlled_buffer_2_out);
  not not_20 (not_20_out, controlled_buffer_5_out);
  not not_21 (not_21_out, controlled_buffer_4_out);
  not not_22 (not_22_out, controlled_buffer_5_out);
  not not_23 (not_23_out, controlled_buffer_2_out);
  not not_24 (not_24_out, controlled_buffer_4_out);
  not not_25 (not_25_out, controlled_buffer_3_out);
  not not_26 (not_26_out, controlled_buffer_3_out);
  not not_27 (not_27_out, controlled_buffer_2_out);
  not not_28 (not_28_out, controlled_buffer_1_out);
  not not_29 (not_29_out, controlled_buffer_5_out);
  not not_30 (not_30_out, controlled_buffer_4_out);
  not not_31 (not_31_out, controlled_buffer_3_out);
  and and_2 (and_2_out, not_1_out, not_2_out, not_3_out, not_4_out, controlled_buffer_2_out);
  and and_3 (and_3_out, not_5_out, not_6_out, controlled_buffer_4_out, not_7_out, not_8_out);
  and and_4 (and_4_out, not_9_out, not_10_out, controlled_buffer_4_out, controlled_buffer_3_out, controlled_buffer_2_out);
  and and_5 (and_5_out, not_11_out, controlled_buffer_5_out, not_12_out, controlled_buffer_3_out, not_13_out);
  and and_6 (and_6_out, not_14_out, controlled_buffer_5_out, controlled_buffer_4_out, not_15_out, controlled_buffer_2_out);
  and and_7 (and_7_out, controlled_buffer_1_out, not_16_out, not_17_out, not_18_out, not_19_out);
  and and_8 (and_8_out, controlled_buffer_1_out, not_20_out, not_21_out, controlled_buffer_3_out, controlled_buffer_2_out);
  and and_9 (and_9_out, controlled_buffer_1_out, not_22_out, controlled_buffer_4_out, controlled_buffer_3_out, not_23_out);
  and and_10 (and_10_out, controlled_buffer_1_out, controlled_buffer_5_out, not_24_out, not_25_out, controlled_buffer_2_out);
  and and_11 (and_11_out, controlled_buffer_1_out, controlled_buffer_5_out, controlled_buffer_4_out, not_26_out, not_27_out);
  and and_12 (and_12_out, not_28_out, not_29_out, not_30_out, not_31_out, controlled_buffer_2_out);
  or or_2 (R1, and_2_out, and_3_out, and_4_out, and_5_out, and_6_out, and_7_out, and_8_out, and_9_out, and_10_out, and_11_out, and_12_out);
endmodule

module \_1_нуль  (
  input  B0,
  input  B1,
  input  B2,
  input  B3,
  input  B4,
  output Dont_care,
  output R1
);

  wire and_1_out, and_2_out, and_3_out, and_4_out, and_5_out, and_6_out, and_7_out, and_8_out, and_9_out,
       and_10_out, and_11_out, and_12_out, and_13_out, controlled_buffer_1_out, controlled_buffer_2_out,
       controlled_buffer_3_out, controlled_buffer_4_out, controlled_buffer_5_out, nor_1_out, nor_2_out,
       not_1_out, not_2_out, not_3_out, not_4_out, not_5_out, not_6_out, not_7_out, not_8_out, not_9_out,
       not_10_out, not_11_out, not_12_out, not_13_out, not_14_out, not_15_out, not_16_out, not_17_out,
       not_18_out, not_19_out, not_20_out, not_21_out, not_22_out, not_23_out, not_24_out, not_25_out,
       not_26_out, not_27_out;

  and and_1 (and_1_out, B4, B2, B3, B1, B0);
  nor nor_1 (nor_1_out, and_1_out, nor_2_out);
  nor nor_2 (nor_2_out, B4, B2, B3, B1, B0);
  or or_1 (Dont_care, nor_2_out, and_1_out);
  assign controlled_buffer_1_out = nor_1_out ? B2 : 1'bz;  // Controlled_Buffer controlled_buffer_1
  assign controlled_buffer_2_out = nor_1_out ? B4 : 1'bz;  // Controlled_Buffer controlled_buffer_2
  assign controlled_buffer_3_out = nor_1_out ? B1 : 1'bz;  // Controlled_Buffer controlled_buffer_3
  assign controlled_buffer_4_out = nor_1_out ? B3 : 1'bz;  // Controlled_Buffer controlled_buffer_4
  assign controlled_buffer_5_out = nor_1_out ? B0 : 1'bz;  // Controlled_Buffer controlled_buffer_5
  not not_1 (not_1_out, controlled_buffer_2_out);
  not not_2 (not_2_out, controlled_buffer_4_out);
  not not_3 (not_3_out, controlled_buffer_3_out);
  not not_4 (not_4_out, controlled_buffer_2_out);
  not not_5 (not_5_out, controlled_buffer_1_out);
  not not_6 (not_6_out, controlled_buffer_3_out);
  not not_7 (not_7_out, controlled_buffer_5_out);
  not not_8 (not_8_out, controlled_buffer_2_out);
  not not_9 (not_9_out, controlled_buffer_1_out);
  not not_10 (not_10_out, controlled_buffer_5_out);
  not not_11 (not_11_out, controlled_buffer_2_out);
  not not_12 (not_12_out, controlled_buffer_4_out);
  not not_13 (not_13_out, controlled_buffer_1_out);
  not not_14 (not_14_out, controlled_buffer_5_out);
  not not_15 (not_15_out, controlled_buffer_4_out);
  not not_16 (not_16_out, controlled_buffer_3_out);
  not not_17 (not_17_out, controlled_buffer_5_out);
  not not_18 (not_18_out, controlled_buffer_4_out);
  not not_19 (not_19_out, controlled_buffer_1_out);
  not not_20 (not_20_out, controlled_buffer_3_out);
  not not_21 (not_21_out, controlled_buffer_5_out);
  not not_22 (not_22_out, controlled_buffer_2_out);
  not not_23 (not_23_out, controlled_buffer_3_out);
  not not_24 (not_24_out, controlled_buffer_5_out);
  not not_25 (not_25_out, controlled_buffer_2_out);
  not not_26 (not_26_out, controlled_buffer_4_out);
  not not_27 (not_27_out, controlled_buffer_5_out);
  and and_2 (and_2_out, not_1_out, not_2_out, controlled_buffer_1_out, not_3_out, controlled_buffer_5_out);
  and and_3 (and_3_out, not_4_out, controlled_buffer_4_out, not_5_out, not_6_out, not_7_out);
  and and_4 (and_4_out, not_8_out, controlled_buffer_4_out, not_9_out, controlled_buffer_3_out, not_10_out);
  and and_5 (and_5_out, not_11_out, controlled_buffer_4_out, controlled_buffer_1_out, controlled_buffer_3_out, controlled_buffer_5_out);
  and and_6 (and_6_out, controlled_buffer_2_out, not_12_out, not_13_out, controlled_buffer_3_out, not_14_out);
  and and_7 (and_7_out, controlled_buffer_2_out, not_15_out, controlled_buffer_1_out, not_16_out, not_17_out);
  and and_8 (and_8_out, controlled_buffer_2_out, not_18_out, controlled_buffer_1_out, controlled_buffer_3_out, controlled_buffer_5_out);
  and and_9 (and_9_out, controlled_buffer_2_out, controlled_buffer_4_out, not_19_out, controlled_buffer_3_out, controlled_buffer_5_out);
  and and_10 (and_10_out, controlled_buffer_2_out, controlled_buffer_4_out, controlled_buffer_1_out, not_20_out, controlled_buffer_5_out);
  and and_11 (and_11_out, controlled_buffer_2_out, controlled_buffer_4_out, controlled_buffer_1_out, controlled_buffer_3_out, not_21_out);
  and and_12 (and_12_out, not_22_out, controlled_buffer_4_out, not_23_out, not_24_out);
  and and_13 (and_13_out, not_25_out, not_26_out, controlled_buffer_3_out, not_27_out);
  or or_2 (R1, and_2_out, and_3_out, and_4_out, and_5_out, and_6_out, and_7_out, and_8_out, and_9_out, and_10_out, and_11_out, and_12_out, and_13_out);
endmodule

module \_2_нуля  (
  input  B0,
  input  B1,
  input  B2,
  input  B3,
  input  B4,
  output R1,
  output Dont_care
);

  wire and_1_out, and_2_out, and_3_out, and_4_out, and_5_out, and_6_out, and_7_out, controlled_buffer_1_out,
       controlled_buffer_2_out, controlled_buffer_3_out, controlled_buffer_4_out, controlled_buffer_5_out,
       nor_1_out, nor_2_out, not_1_out, not_2_out, not_3_out, not_4_out, not_5_out, not_6_out, not_7_out,
       not_8_out, not_9_out, not_10_out, not_11_out, not_12_out;

  and and_1 (and_1_out, B4, B3, B2, B1, B0);
  nor nor_1 (nor_1_out, B4, B3, B2, B1, B0);
  nor nor_2 (nor_2_out, and_1_out, nor_1_out);
  or or_1 (Dont_care, nor_1_out, and_1_out);
  assign controlled_buffer_1_out = nor_2_out ? B3 : 1'bz;  // Controlled_Buffer controlled_buffer_1
  assign controlled_buffer_2_out = nor_2_out ? B4 : 1'bz;  // Controlled_Buffer controlled_buffer_2
  assign controlled_buffer_3_out = nor_2_out ? B0 : 1'bz;  // Controlled_Buffer controlled_buffer_3
  assign controlled_buffer_4_out = nor_2_out ? B1 : 1'bz;  // Controlled_Buffer controlled_buffer_4
  assign controlled_buffer_5_out = nor_2_out ? B2 : 1'bz;  // Controlled_Buffer controlled_buffer_5
  not not_1 (not_1_out, controlled_buffer_2_out);
  not not_2 (not_2_out, controlled_buffer_5_out);
  not not_3 (not_3_out, controlled_buffer_2_out);
  not not_4 (not_4_out, controlled_buffer_4_out);
  not not_5 (not_5_out, controlled_buffer_2_out);
  not not_6 (not_6_out, controlled_buffer_3_out);
  not not_7 (not_7_out, controlled_buffer_1_out);
  not not_8 (not_8_out, controlled_buffer_4_out);
  not not_9 (not_9_out, controlled_buffer_1_out);
  not not_10 (not_10_out, controlled_buffer_3_out);
  not not_11 (not_11_out, controlled_buffer_5_out);
  not not_12 (not_12_out, controlled_buffer_3_out);
  and and_2 (and_2_out, not_1_out, controlled_buffer_1_out, not_2_out, controlled_buffer_4_out);
  and and_3 (and_3_out, not_3_out, controlled_buffer_1_out, controlled_buffer_5_out, not_4_out, controlled_buffer_3_out);
  and and_4 (and_4_out, not_5_out, controlled_buffer_1_out, controlled_buffer_5_out, controlled_buffer_4_out, not_6_out);
  and and_5 (and_5_out, controlled_buffer_2_out, not_7_out, controlled_buffer_5_out, not_8_out, controlled_buffer_3_out);
  and and_6 (and_6_out, controlled_buffer_2_out, not_9_out, controlled_buffer_5_out, controlled_buffer_4_out, not_10_out);
  and and_7 (and_7_out, controlled_buffer_2_out, controlled_buffer_1_out, not_11_out, controlled_buffer_4_out, not_12_out);
  or or_2 (R1, and_2_out, and_3_out, and_4_out, and_5_out, and_6_out, and_7_out);
endmodule

module \LF_реализации  (
  input  B1,
  input  B2,
  input  B3,
  input  B4,
  input  B5,
  output R1,
  output R2,
  output F1,
  output F2
);

  wire and_1_out, and_2_out, and_3_out, and_4_out, and_5_out, and_6_out, and_7_out, and_8_out, and_9_out,
       and_10_out, and_11_out, and_12_out, and_13_out, and_14_out, and_15_out, and_16_out, and_17_out,
       and_18_out, and_19_out, and_20_out, and_21_out, and_22_out, and_23_out, and_24_out, and_25_out,
       and_26_out, and_27_out, and_28_out, and_29_out, and_30_out, and_31_out, and_32_out, and_33_out,
       and_34_out, and_35_out, and_36_out, and_37_out, and_38_out, and_39_out, and_40_out, and_41_out,
       and_42_out, not_1_out, not_2_out, not_3_out, not_4_out, not_5_out, not_6_out, not_7_out, not_8_out,
       not_9_out, not_10_out, not_11_out, not_12_out, not_13_out, not_14_out, not_15_out, not_16_out,
       not_17_out, not_18_out, not_19_out, not_20_out, not_21_out, not_22_out, not_23_out, not_24_out,
       not_25_out, not_26_out, not_27_out, not_28_out, not_29_out, not_30_out, not_31_out, not_32_out,
       not_33_out, not_34_out, not_35_out, not_36_out, not_37_out, not_38_out, not_39_out, not_40_out,
       not_41_out, not_42_out, not_43_out, not_44_out, not_45_out, not_46_out, not_47_out, not_48_out,
       not_49_out, not_50_out, not_51_out, not_52_out, not_53_out, not_54_out, not_55_out, not_56_out,
       not_57_out, not_58_out, not_59_out, not_60_out, not_61_out, not_62_out, not_63_out, not_64_out,
       not_65_out, not_66_out, not_67_out, not_68_out, not_69_out, not_70_out, not_71_out, not_72_out,
       not_73_out, not_74_out, not_75_out, not_76_out, not_77_out, not_78_out, not_79_out, not_80_out,
       not_81_out, not_82_out, not_83_out, not_84_out, not_85_out, not_86_out, not_87_out, not_88_out,
       not_89_out, not_90_out, not_91_out, not_92_out, not_93_out, not_94_out, not_95_out, not_96_out,
       not_97_out, not_98_out;

  not not_1 (not_1_out, B1);
  not not_2 (not_2_out, B2);
  not not_3 (not_3_out, B3);
  not not_4 (not_4_out, B4);
  not not_5 (not_5_out, B1);
  not not_6 (not_6_out, B2);
  not not_7 (not_7_out, B4);
  not not_8 (not_8_out, B5);
  not not_9 (not_9_out, B1);
  not not_10 (not_10_out, B2);
  not not_11 (not_11_out, B1);
  not not_12 (not_12_out, B3);
  not not_13 (not_13_out, B5);
  not not_14 (not_14_out, B1);
  not not_15 (not_15_out, B4);
  not not_16 (not_16_out, B2);
  not not_17 (not_17_out, B3);
  not not_18 (not_18_out, B4);
  not not_19 (not_19_out, B5);
  not not_20 (not_20_out, B2);
  not not_21 (not_21_out, B3);
  not not_22 (not_22_out, B2);
  not not_23 (not_23_out, B5);
  not not_24 (not_24_out, B3);
  not not_25 (not_25_out, B4);
  not not_26 (not_26_out, B4);
  not not_27 (not_27_out, B5);
  not not_28 (not_28_out, B1);
  not not_29 (not_29_out, B2);
  not not_30 (not_30_out, B3);
  not not_31 (not_31_out, B5);
  not not_32 (not_32_out, B1);
  not not_33 (not_33_out, B2);
  not not_34 (not_34_out, B4);
  not not_35 (not_35_out, B1);
  not not_36 (not_36_out, B3);
  not not_37 (not_37_out, B4);
  not not_38 (not_38_out, B5);
  not not_39 (not_39_out, B1);
  not not_40 (not_40_out, B3);
  not not_41 (not_41_out, B1);
  not not_42 (not_42_out, B5);
  not not_43 (not_43_out, B2);
  not not_44 (not_44_out, B3);
  not not_45 (not_45_out, B4);
  not not_46 (not_46_out, B2);
  not not_47 (not_47_out, B4);
  not not_48 (not_48_out, B5);
  not not_49 (not_49_out, B2);
  not not_50 (not_50_out, B3);
  not not_51 (not_51_out, B5);
  not not_52 (not_52_out, B4);
  not not_53 (not_53_out, B1);
  not not_54 (not_54_out, B2);
  not not_55 (not_55_out, B3);
  not not_56 (not_56_out, B5);
  not not_57 (not_57_out, B1);
  not not_58 (not_58_out, B2);
  not not_59 (not_59_out, B4);
  not not_60 (not_60_out, B1);
  not not_61 (not_61_out, B2);
  not not_62 (not_62_out, B5);
  not not_63 (not_63_out, B1);
  not not_64 (not_64_out, B3);
  not not_65 (not_65_out, B4);
  not not_66 (not_66_out, B5);
  not not_67 (not_67_out, B1);
  not not_68 (not_68_out, B3);
  not not_69 (not_69_out, B4);
  not not_70 (not_70_out, B1);
  not not_71 (not_71_out, B3);
  not not_72 (not_72_out, B5);
  not not_73 (not_73_out, B1);
  not not_74 (not_74_out, B4);
  not not_75 (not_75_out, B5);
  not not_76 (not_76_out, B1);
  not not_77 (not_77_out, B2);
  not not_78 (not_78_out, B3);
  not not_79 (not_79_out, B5);
  not not_80 (not_80_out, B2);
  not not_81 (not_81_out, B4);
  not not_82 (not_82_out, B5);
  not not_83 (not_83_out, B2);
  not not_84 (not_84_out, B3);
  not not_85 (not_85_out, B4);
  not not_86 (not_86_out, B5);
  not not_87 (not_87_out, B1);
  not not_88 (not_88_out, B3);
  not not_89 (not_89_out, B1);
  not not_90 (not_90_out, B4);
  not not_91 (not_91_out, B5);
  not not_92 (not_92_out, B1);
  not not_93 (not_93_out, B5);
  not not_94 (not_94_out, B1);
  not not_95 (not_95_out, B2);
  not not_96 (not_96_out, B5);
  not not_97 (not_97_out, B2);
  not not_98 (not_98_out, B3);
  and and_1 (and_1_out, not_1_out, not_2_out, not_3_out, not_4_out, B5);
  and and_2 (and_2_out, not_5_out, not_6_out, B3, not_7_out, not_8_out);
  and and_3 (and_3_out, not_9_out, not_10_out, B3, B4, B5);
  and and_4 (and_4_out, not_11_out, B2, not_12_out, B4, not_13_out);
  and and_5 (and_5_out, not_14_out, B2, B3, not_15_out, B5);
  and and_6 (and_6_out, B1, not_16_out, not_17_out, not_18_out, not_19_out);
  and and_7 (and_7_out, B1, not_20_out, not_21_out, B4, B5);
  and and_8 (and_8_out, B1, not_22_out, B3, B4, not_23_out);
  and and_9 (and_9_out, B1, B2, not_24_out, not_25_out, B5);
  and and_10 (and_10_out, B1, B2, B3, not_26_out, not_27_out);
  and and_11 (and_11_out, B1, B2, B3, B4, B5);
  and and_12 (and_12_out, not_28_out, not_29_out, not_30_out, B4, not_31_out);
  and and_13 (and_13_out, not_32_out, not_33_out, B3, not_34_out, B5);
  and and_14 (and_14_out, not_35_out, B2, not_36_out, not_37_out, not_38_out);
  and and_15 (and_15_out, not_39_out, B2, not_40_out, B4, B5);
  and and_16 (and_16_out, not_41_out, B2, B3, B4, not_42_out);
  and and_17 (and_17_out, B1, not_43_out, not_44_out, not_45_out, B5);
  and and_18 (and_18_out, B1, not_46_out, B3, not_47_out, not_48_out);
  and and_19 (and_19_out, B1, not_49_out, B3, B4, B5);
  and and_20 (and_20_out, B1, B2, not_50_out, B4, not_51_out);
  and and_21 (and_21_out, B1, B2, B3, not_52_out, B5);
  and and_22 (and_22_out, not_53_out, not_54_out, not_55_out, B4, not_56_out);
  and and_23 (and_23_out, not_57_out, not_58_out, B3, not_59_out, B5);
  and and_24 (and_24_out, not_60_out, not_61_out, B3, B4, not_62_out);
  and and_25 (and_25_out, not_63_out, B2, not_64_out, not_65_out, not_66_out);
  and and_26 (and_26_out, not_67_out, B2, not_68_out, not_69_out, B5);
  and and_27 (and_27_out, not_70_out, B2, not_71_out, B4, not_72_out);
  and and_28 (and_28_out, not_73_out, B2, B3, not_74_out, not_75_out);
  and and_29 (and_29_out, not_76_out, B2, B3, B4, B5);
  and and_30 (and_30_out, B1, not_77_out, not_78_out, B4, not_79_out);
  and and_31 (and_31_out, B1, not_80_out, B3, not_81_out, not_82_out);
  and and_32 (and_32_out, B1, not_83_out, B3, B4, B5);
  and and_33 (and_33_out, B1, B2, not_84_out, B4, B5);
  and and_34 (and_34_out, B1, B2, B3, not_85_out, B5);
  and and_35 (and_35_out, B1, B2, B3, B4, not_86_out);
  and and_36 (and_36_out, not_87_out, B2, not_88_out, B4, B5);
  and and_37 (and_37_out, not_89_out, B2, B3, not_90_out, not_91_out);
  and and_38 (and_38_out, not_92_out, B2, B3, B4, not_93_out);
  and and_39 (and_39_out, not_94_out, B2, B3, B4, B5);
  and and_40 (and_40_out, B1, not_95_out, B3, B4, not_96_out);
  and and_41 (and_41_out, B1, not_97_out, B3, B4, B5);
  and and_42 (and_42_out, B1, B2, not_98_out, B4, B5);
  or or_1 (R1, and_1_out, and_2_out, and_3_out, and_4_out, and_5_out, and_6_out, and_7_out, and_8_out, and_9_out, and_10_out, and_11_out);
  or or_2 (R2, and_12_out, and_13_out, and_14_out, and_15_out, and_16_out, and_17_out, and_18_out, and_19_out, and_20_out, and_21_out);
  or or_3 (F1, and_22_out, and_23_out, and_24_out, and_25_out, and_26_out, and_27_out, and_28_out, and_29_out, and_30_out, and_31_out, and_32_out, and_33_out, and_34_out, and_35_out);
  or or_4 (F2, and_36_out, and_37_out, and_38_out, and_39_out, and_40_out, and_41_out, and_42_out);
endmodule
