// Logisim project ABC6.circ as structural Verilog: 4 circuits, main circuit main
module main (
  input  X4,
  input  Y4,
  input  X3,
  input  Y3,
  input  X2,
  input  Y2,
  input  X1,
  input  Y1,
  input  P0,
  output S5,
  output S4,
  output S3,
  output S2,
  output S1
);

  wire \полный_сумматор_1_p_2 , \полный_сумматор_2_p_2 , \полный_сумматор_3_p_2 ;

  \Полный_сумматор  \u_полный_сумматор_1  (.X1(X1), .X2(Y1), .P(P0), .P_2(\полный_сумматор_1_p_2 ), .S(S1));
  \Полный_сумматор  \u_полный_сумматор_2  (
    .X1(X3), .X2(Y3), .P(\полный_сумматор_3_p_2 ), .P_2(\полный_сумматор_2_p_2 ), .S(S3));
  \Полный_сумматор  \u_полный_сумматор_3  (
    .X1(X2), .X2(Y2), .P(\полный_сумматор_1_p_2 ), .P_2(\полный_сумматор_3_p_2 ), .S(S2));
  \Полный_сумматор  \u_полный_сумматор_4  (.X1(X4), .X2(Y4), .P(\полный_сумматор_2_p_2 ), .P_2(S5), .S(S4));

  // Notes on the sheet:
  //   P1
  //   Схема 4 сумматоров
  //   P3
  //   P2
  //   P4
endmodule

module \Схема_сравнения  (
  input  X1,
  input  X2,
  output Y
);

  wire \И_2_out , \И_out , \НЕ_2_out , \НЕ_out ;

  not \u_НЕ  (\НЕ_out , X1);
  not \u_НЕ_2  (\НЕ_2_out , X2);
  and \u_И  (\И_out , \НЕ_out , X2);
  and \u_И_2  (\И_2_out , X1, \НЕ_2_out );
  or \u_ИЛИ  (Y, \И_out , \И_2_out );

  // Notes on the sheet:
  //   Схема сравнения
endmodule

module \Полусумматор  (
  input  X1,
  input  X2,
  output \Старший_разряд___перенос ,
  output \Младший_разряд 
);

  and \u_И  (\Старший_разряд___перенос , X1, X2);
  \Схема_сравнения  \u_Схема_сравнения  (.X1(X1), .X2(X2), .Y(\Младший_разряд ));

  // Notes on the sheet:
  //   Полусумматор
endmodule

// SM
module \Полный_сумматор  (
  input  X1,
  input  X2,
  input  P,
  output P_2,
  output S
);

  wire \Полусумматор_2_старший_разряд___перенос , \Полусумматор_младший_разряд ,
       \Полусумматор_старший_разряд___перенос ;

  \Полусумматор  \u_Полусумматор  (
    .X1(X1), .X2(X2), .\Старший_разряд___перенос (\Полусумматор_старший_разряд___перенос ),
    .\Младший_разряд (\Полусумматор_младший_разряд ));
  \Полусумматор  \u_Полусумматор_2  (
    .X1(\Полусумматор_младший_разряд ), .X2(P),
    .\Старший_разряд___перенос (\Полусумматор_2_старший_разряд___перенос ), .\Младший_разряд (S));
  or \u_ИЛИ  (P_2, \Полусумматор_старший_разряд___перенос , \Полусумматор_2_старший_разряд___перенос );

  // Notes on the sheet:
  //   Сумматор
  //   Перенос
  //   Младший разряд суммы
endmodule
